# Fritzing sketch DIY Meshtastic PCB 30Pin vertical (saved by Fritzing 0.9.3b)
circuit board: 5cm x 10.6cm
breadboards: 1

parts:
  E22-900M30S1 = E22-900M30S [part_number=E22-900M30S]
  C6 = Ceramic Capacitor [capacitance=100nF package="100 mil [THT, multilayer]"]
  C7 = Capacitor Polarized [package=cpol-radial-100uf-25v]
  C8 = Ceramic Capacitor [capacitance=100nF package="100 mil [THT, multilayer]"]
  C9 = Capacitor Polarized [package=cpol-radial-100uf-25v]
  R2 = Resistor [tolerance=±5% resistance=10k package=THT]
  C10 = Ceramic Capacitor [capacitance=100nF package="100 mil [THT, multilayer]"]
  GNSS = IC, SIP package, 4 pins [chip_label=IC]
  oled = IC, SIP package, 4 pins [chip_label=IC]
  button = SIP - 2 pins [chip_label=IC package="SIP (Single Inline) [THT]"]
  ESP32_Devkit_(30-pin)1 = DOIT Esp32 DevKit v1 (30 pins long, 11 pins width) [part_number=ESP32S-PIN30]

nets:
  N1: E22-900M30S1.Pin_1, E22-900M30S1.Pin_2, E22-900M30S1.Pin_3, E22-900M30S1.Pin_5, E22-900M30S1.Pin_11, E22-900M30S1.Pin_12, E22-900M30S1.Pin_22, C10.0
  N2: E22-900M30S1.Pin_9, C10.1
  N3: C6.0, C7.-, GNSS.pin4, ESP32_Devkit_(30-pin)1.GND
  N4: C6.1, C7.+, GNSS.pin1
  N5: C8.0, C9.-, oled.pin1
  N6: C8.1, C9.+, R2.Pin_0, oled.pin2
  N7: R2.Pin_1, button.pin1

notes:
  5v    TX  G
  GNSS
  100uF
  100nF
  G 3v SCL SDA
  Oled
  10k
  E22-XXXM30S
  30 Pin ESP32
  BTN

custom parts:
  E22-900M30S: The E22-900M30S is based on the SX1262, a new generation of LoRaTM RF chip manufactured by Semtech, USA. It is an ultra-small and self-developed 868MHz, 915MHz SMD LoRaTM wireless module..
  DOIT Esp32 DevKit v1 (30 pins long, 11 pins width): The DOIT Esp32 DevKit v1 is one of the development board created by DOIT to evaluate the ESP-WROOM-32 module. It is based on the ESP32 microcontroller that boasts Wifi, Bluetooth, Ethernet and Low Power support all in a single chip. (vanepp) made breadboard work, adjusted pin numbering and labels and reduced size of schematic and cleaned up pcb. This chip is 30pins long (2 x15) and 11 pins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
