# Fritzing sketch DIY Meshtastic PCB 38 pin vertical (saved by Fritzing 0.9.3b)
circuit board: 5cm x 10.6cm
breadboards: 1

parts:
  E22-900M30S2 = E22-900M30S [part_number=E22-900M30S]
  C1 = Ceramic Capacitor [capacitance=100nF package="100 mil [THT, multilayer]"]
  GPS1 = IC, SIP package, 4 pins [chip_label=IC]
  oled1 = IC, SIP package, 4 pins [chip_label=IC]
  button = SIP - 2 pins [chip_label=IC package="SIP (Single Inline) [THT]"]
  C4 = Capacitor Polarized [package=cpol-radial-100uf-25v]
  C5 = Ceramic Capacitor [capacitance=100nF package="100 mil [THT, multilayer]"]
  C6 = Capacitor Polarized [package=cpol-radial-100uf-25v]
  R1 = Resistor [tolerance=±5% resistance=10k package=THT]
  U1 = ESP32-38PinWide [part_number=ESP32-38PinWide]
  C3 = Ceramic Capacitor [capacitance=100nF package="100 mil [THT, multilayer]"]

nets (from the pcb view):
  N1: E22-900M30S2.Pin_1, E22-900M30S2.Pin_11, E22-900M30S2.Pin_22, C1.0, GPS1.pin4, oled1.pin1, button.pin2, C4.-, C5.0, C6.-, U1.GND, C3.0
  N2: E22-900M30S2.Pin_6, U1.GPIO14
  N3: E22-900M30S2.Pin_7, U1.GPIO13
  N4: E22-900M30S2.Pin_9, E22-900M30S2.Pin_10, C1.1, GPS1.pin1, C5.1, C6.+, U1.VIN
  N5: E22-900M30S2.Pin_13, U1.GPIO33
  N6: E22-900M30S2.Pin_14, U1.GPIO32
  N7: E22-900M30S2.Pin_15, U1.GPIO23
  N8: E22-900M30S2.Pin_16, U1.GPIO19
  N9: E22-900M30S2.Pin_17, U1.GPIO16
  N10: E22-900M30S2.Pin_18, U1.GPIO5
  N11: E22-900M30S2.Pin_19, U1.GPIO18
  N12: GPS1.pin3, U1.GPIO15
  N13: oled1.pin2, C4.+, R1.Pin_0, U1.3.3, C3.1
  N14: oled1.pin3, U1.GPIO22
  N15: oled1.pin4, U1.GPIO21
  N16: button.pin1, R1.Pin_1, U1.GPIO39

notes:
  Oled
  G 3v SCL SDA
  5v    TX  G
  GNSS
  BTN
  10k
  100uF
  100nF
  38 Pin ESP32
  E22-XXXM30S

custom parts:
  E22-900M30S: The E22-900M30S is based on the SX1262, a new generation of LoRaTM RF chip manufactured by Semtech, USA. It is an ultra-small and self-developed 868MHz, 915MHz SMD LoRaTM wireless module..
  ESP32-38PinWide: Generic 38-Pin ESP32 with wide format (only access to one side of pins on a breadboard) based on Stephen Lilley's HiLetgo ESP-WROOM-32 ESP32 ESP-32S Development Board.
